# Fritzing sketch Esquema Eletrico (saved by Fritzing 0.9.6b)

parts:
  IR_Transmitter_5mm = smd LED [color="White (8000K)" package="1206 [SMD]"]
  IR_Receiver_5mm = smd LED [color="Infrared (940nm)" package="1206 [SMD]"]
  IR_Receiver_5mm_2 = smd LED [color="Infrared (940nm)" package="1206 [SMD]"]
  IR_Receiver_5mm_3 = smd LED [color="Infrared (940nm)" package="1206 [SMD]"]
  IR_Transmitter_5mm_2 = smd LED [color="White (8000K)" package="1206 [SMD]"]
  IR_Transmitter_5mm_3 = smd LED [color="White (8000K)" package="1206 [SMD]"]
  Arduino_UNO_(Rev3) = Arduino Uno (Rev3) - ICSP  # not connected
  DFRobot_-_LCD_Keypad_Shield = LCD Keypad Shield
  Resistor_10kΩ = Resistor [tolerance=±10% resistance=10k package="2512 [SMD]"]
  Resistor_10kΩ_2 = Resistor [tolerance=±10% resistance=10k package="2512 [SMD]"]
  Resistor_10kΩ_3 = Resistor [tolerance=±10% resistance=10k package="2512 [SMD]"]
  Resistor_220Ω = Resistor [tolerance=±20% resistance=220 package="2512 [SMD]"]
  Servo_Motor = Basic Servo
  IR_Receiver_5mm_4 = smd LED [color="Infrared (940nm)" package="1206 [SMD]"]
  IR_Transmitter_5mm_4 = smd LED [color="White (8000K)" package="1206 [SMD]"]
  Resistor_10kΩ_4 = Resistor [tolerance=±10% resistance=10k package="2512 [SMD]"]

nets:
  N1: IR_Transmitter_5mm.cathode, IR_Transmitter_5mm_2.cathode, IR_Transmitter_5mm_3.cathode
  N2: IR_Transmitter_5mm.anode, IR_Transmitter_5mm_2.anode, IR_Transmitter_5mm_3.anode, Resistor_220Ω.Pin_1
  GND: IR_Receiver_5mm.cathode, IR_Receiver_5mm_2.cathode, IR_Receiver_5mm_3.cathode, DFRobot_-_LCD_Keypad_Shield.GND, Servo_Motor.gnd
  N3: IR_Receiver_5mm.anode, DFRobot_-_LCD_Keypad_Shield.A2, Resistor_10kΩ_2.Pin_1
  N4: IR_Receiver_5mm_2.anode, DFRobot_-_LCD_Keypad_Shield.A1, Resistor_10kΩ.Pin_1, IR_Transmitter_5mm_4.anode
  N5: IR_Receiver_5mm_3.anode, DFRobot_-_LCD_Keypad_Shield.A3, Resistor_10kΩ_3.Pin_0
  N6: DFRobot_-_LCD_Keypad_Shield.A4(SDA), Servo_Motor.pulse
  N7: DFRobot_-_LCD_Keypad_Shield.A5(CLK), IR_Receiver_5mm_4.anode, Resistor_10kΩ_4.Pin_0
  +5V: DFRobot_-_LCD_Keypad_Shield.+5V, Resistor_10kΩ.Pin_0, Resistor_10kΩ_2.Pin_0, Resistor_10kΩ_3.Pin_1, Resistor_220Ω.Pin_0, Servo_Motor.vcc, Resistor_10kΩ_4.Pin_1
  N8: IR_Receiver_5mm_4.cathode, IR_Transmitter_5mm_4.cathode

custom parts:
  LCD Keypad Shield: It consists of a 1602 white character blue backlight LCD. The keypad consists of 5 keys — select, up, right, down and left. To save the digital IO pins, the keypad interface uses only one ADC channel. The key value is read through a 5 stage voltage divider.
